// Logisim project cpu.circ as structural Verilog: 7 circuits, main circuit main
module main (
  input  [15:0] From_Instr_Mem,
  input  clk,
  input  in_3,
  output [15:0] r0,
  output [15:0] r1,
  output [15:0] r2,
  output [15:0] r3,
  output [15:0] Display_0,
  output [15:0] Display_1,
  output [15:0] To_Instr_Mem,
  output [15:0] Data_Mem_Data,
  output [15:0] Data_Mem_Addr,
  output Data_Mem_Write
);

  wire and_1_out, and_2_out, bc, beq, bne, Display, exec_instruction_1_equal,
       exec_instruction_1_signed_overflow, ffo, Imm, jal, jr, jump_jal, lui, MemToReg, nop, not_1_out,
       not_2_out, not_3_out, or_1_out, or_3_out, RegDst, RegWrite, \signed , zb;
  wire [1:0] multiplexer_6_out, multiplexer_8_out, rd, rs, rt;
  wire [3:0] opcode;
  wire [5:0] funct;
  wire [7:0] controlled_buffer_2_out, imm_t;
  wire [11:0] target_address;
  wire [15:0] adder_1_out, adder_2_out, ALU_1, ALU_2, bc_1_rt, bit_extender_1_out, demultiplexer_1_out0,
       demultiplexer_1_out1, ffo_1_rt, ffo_zb_bc_result, multiplexer_1_out, multiplexer_2_out,
       multiplexer_3_out, multiplexer_4_out, multiplexer_5_out, multiplexer_7_out, multiplexer_9_out,
       multiplexer_10_out, multiplexer_11_out, multiplexer_12_out, multiplexer_13_out, multiplexer_14_out,
       multiplexer_16_out, multiplexer_17_out, offset, RAM, register_2_q, shifter_1_out, zb_1_rt;

  Register #(.width(16)) register_1 (.D(multiplexer_5_out), .Q(To_Instr_Mem), .clk(clk));  // open: en, clr
  Control control_1 (
    .opcode(opcode), .RegDst(RegDst), .ffo(ffo), .zb(zb), .bc(bc), .\signed (\signed ), .Imm(Imm),
    .MemToReg(MemToReg), .RegWrite(RegWrite), .jal(jal), .jump_jal(jump_jal), .jr(jr), .bne(bne), .beq(beq),
    .MemWrite(Data_Mem_Write), .lui(lui), .Display(Display));
  LED led_1 (.in(exec_instruction_1_signed_overflow));
  Exec_Instruction exec_instruction_1 (
    .X(ALU_1), .Y(ALU_2), .funct(funct[3:0]), .opcode(opcode),
    .Signed_Overflow(exec_instruction_1_signed_overflow), .Result(Data_Mem_Addr),
    .Equal(exec_instruction_1_equal));
  Adder #(.width(16)) adder_1 (.a(To_Instr_Mem), .b(16'h1), .out(adder_1_out));  // open: cin, cout
  or or_1 (or_1_out, jump_jal, jr, jal, nop);
  not not_1 (not_1_out, exec_instruction_1_equal);
  Multiplexer #(.width(16)) multiplexer_1 (
    .in0(adder_1_out), .in1(To_Instr_Mem), .out(multiplexer_1_out), .sel(nop));  // open: en
  Register #(.width(16)) register_2 (.D(multiplexer_2_out), .Q(register_2_q), .clk(clk));  // open: en, clr
  Multiplexer #(.width(16)) multiplexer_2 (
    .in0(From_Instr_Mem), .in1({16{1'b0}}), .out(multiplexer_2_out), .sel(or_1_out));  // open: en
  and and_1 (and_1_out, not_1_out, bne);
  or or_2 (nop, and_1_out, and_2_out);
  and and_2 (and_2_out, exec_instruction_1_equal, beq);
  Multiplexer #(.width(16)) multiplexer_3 (
    .in0(multiplexer_1_out), .in1(adder_2_out), .out(multiplexer_3_out), .sel(nop));  // open: en
  Adder #(.width(16)) adder_2 (.a(multiplexer_1_out), .b(offset), .out(adder_2_out));  // open: cin, cout
  Instruction_Splitter instruction_splitter_1 (
    .in_1(register_2_q), .funct(funct), .rd(rd), .imm(imm_t), .rt(rt), .rs(rs), .opcode(opcode),
    .target_address(target_address));
  Multiplexer #(.width(16)) multiplexer_4 (
    .in0(multiplexer_3_out), .in1({To_Instr_Mem[15:12], target_address}), .out(multiplexer_4_out),
    .sel(jump_jal));  // open: en
  Multiplexer #(.width(16)) multiplexer_5 (
    .in0(multiplexer_4_out), .in1(ALU_1), .out(multiplexer_5_out), .sel(jr));  // open: en
  Multiplexer #(.width(2), .enable("false")) multiplexer_6 (.in0(rt), .in1(rd), .out(multiplexer_6_out), .sel(RegDst));
  or or_3 (or_3_out, ffo, zb, bc);
  Multiplexer #(.width(16)) multiplexer_7 (
    .in0({16{1'b0}}), .in1(ffo_1_rt), .out(multiplexer_7_out), .sel(ffo));  // open: en
  ffo ffo_1 (.rs(ALU_1), .rt(ffo_1_rt));
  Multiplexer #(.width(2)) multiplexer_8 (
    .in0(multiplexer_6_out), .in1(2'b11), .out(multiplexer_8_out), .sel(jal));  // open: en
  Multiplexer #(.width(16)) multiplexer_9 (
    .in0(multiplexer_10_out), .in1(To_Instr_Mem), .out(multiplexer_9_out), .sel(jal));  // open: en
  Multiplexer #(.width(16)) multiplexer_10 (
    .in0(multiplexer_11_out), .in1(shifter_1_out), .out(multiplexer_10_out), .sel(lui));  // open: en
  Multiplexer #(.width(16)) multiplexer_11 (
    .in0(multiplexer_12_out), .in1(RAM), .out(multiplexer_11_out), .sel(MemToReg));  // open: en
  Multiplexer #(.width(16)) multiplexer_12 (
    .in0(Data_Mem_Addr), .in1(ffo_zb_bc_result), .out(multiplexer_12_out), .sel(or_3_out));  // open: en
  assign ffo_zb_bc_result = multiplexer_7_out | multiplexer_13_out | multiplexer_14_out;  // OR_Gate or_4, 16 bits wide
  Multiplexer #(.width(16)) multiplexer_13 (
    .in0({16{1'b0}}), .in1(zb_1_rt), .out(multiplexer_13_out), .sel(zb));  // open: en
  zb zb_1 (.rs(ALU_1), .rt(zb_1_rt));
  assign RAM = Data_Mem_Write ? Data_Mem_Data : 16'bz;  // Controlled_Buffer controlled_buffer_1
  not not_2 (not_2_out, Data_Mem_Write);
  Multiplexer #(.width(16)) multiplexer_14 (
    .in0({16{1'b0}}), .in1(bc_1_rt), .out(multiplexer_14_out), .sel(bc));  // open: en
  Regfile_main main_1 (
    .Read_register_1(rs), .Read_register_2(rt), .write_register(multiplexer_8_out),
    .write_data(multiplexer_9_out), .Reg_0_Value(r0), .Reg_1_Value(r1), .Reg_2_Value(r2), .Reg_3_Value(r3),
    .RegWrite(RegWrite), .clock(clk), .Read_Data_1(ALU_1), .Read_Data_2(Data_Mem_Data));
  RAM #(.addrWidth(16), .dataWidth(16)) ram_1 (
    .addr(Data_Mem_Addr), .data(RAM), .sel(1'b1), .clk(clk), .ld(not_2_out), .clr(in_3));
  bc bc_1 (.rs(ALU_1), .rt(bc_1_rt));
  Multiplexer #(.width(16)) multiplexer_15 (
    .in0(Data_Mem_Data), .in1(multiplexer_16_out), .out(ALU_2), .sel(Imm));  // open: en
  Shifter #(.width(16)) shifter_1 (.in(multiplexer_16_out), .\dist (4'b1000), .out(shifter_1_out));
  assign bit_extender_1_out = {{8{1'b0}}, imm_t};  // Bit_Extender bit_extender_1
  assign offset = {{8{imm_t[7]}}, imm_t};  // Bit_Extender bit_extender_2
  Multiplexer #(.width(16)) multiplexer_16 (
    .in0(bit_extender_1_out), .in1(offset), .out(multiplexer_16_out), .sel(\signed ));  // open: en
  assign controlled_buffer_2_out = Display ? imm_t : 8'bz;  // Controlled_Buffer controlled_buffer_2
  Multiplexer #(.width(16)) multiplexer_17 (
    .in0({16{1'b0}}), .in1(ALU_1), .out(multiplexer_17_out), .sel(Display));  // open: en
  Demultiplexer #(.width(16), .enable("false")) demultiplexer_1 (
    .out0(demultiplexer_1_out0), .out1(demultiplexer_1_out1), .in(multiplexer_17_out),
    .sel(controlled_buffer_2_out[0]));
  not not_3 (not_3_out, controlled_buffer_2_out[0]);
  Hex_Digit_Display hex_digit_display_1 (.value(Display_0[11:8]));  // open: dp
  Hex_Digit_Display hex_digit_display_2 (.value(Display_0[15:12]));  // open: dp
  Hex_Digit_Display hex_digit_display_3 (.value(Display_0[3:0]));  // open: dp
  Hex_Digit_Display hex_digit_display_4 (.value(Display_0[7:4]));  // open: dp
  Register #(.width(16)) register_3 (.D(demultiplexer_1_out0), .en(not_3_out), .Q(Display_0), .clk(clk));  // open: clr
  Hex_Digit_Display hex_digit_display_5 (.value(Display_1[15:12]));  // open: dp
  Hex_Digit_Display hex_digit_display_6 (.value(Display_1[11:8]));  // open: dp
  Hex_Digit_Display hex_digit_display_7 (.value(Display_1[7:4]));  // open: dp
  Register #(.width(16)) register_4 (
    .D(demultiplexer_1_out1), .en(controlled_buffer_2_out[0]), .Q(Display_1), .clk(clk));  // open: clr
  Hex_Digit_Display hex_digit_display_8 (.value(Display_1[3:0]));  // open: dp

  // Other names for the same wires on the sheet: ALUOut[15:0] = Data_Mem_Addr; Curr_PC[15:0] = To_Instr_Mem;
  //   d0[15:0] = Display_0; d1[15:0] = Display_1; MemWrite = Data_Mem_Write; rtval[15:0] = Data_Mem_Data

  // Notes on the sheet:
  //   Control
  //   This is the current PC that you need to send as OUTPUT
  //   This is the instruction that you would receive as INPUT
  //   Fetch
  //   Remember, this circuit is loaded from the harness to be tested!
  //   This is a CLK that is an INPUT driven from the harness.
  //   DO NOT CHANGE THE LOCATIONS OF THE INPUTS/OUTPUTS! IF YOU DO SO, YOU NEED TO MAKE SURE THE PINS ARE AT THE RIGHT PLACE!
  //   These are OUTPUTS to the circuit
  //   Decode
  //   Memory
  //   Execute
  //   These are OUTPUTS to the circuit
  //   Display
endmodule

module Instruction_Splitter (
  input  [15:0] in_1,
  output [5:0] funct,
  output [1:0] rd,
  output [7:0] imm,
  output [1:0] rt,
  output [1:0] rs,
  output [3:0] opcode,
  output [11:0] target_address
);


  assign funct = in_1[5:0];
  assign imm = in_1[7:0];
  assign opcode = in_1[15:12];
  assign rd = in_1[7:6];
  assign rs = in_1[11:10];
  assign rt = in_1[9:8];
  assign target_address = in_1[11:0];
endmodule

module Control (
  input  [3:0] opcode,
  output RegDst,
  output ffo,
  output zb,
  output bc,
  output \signed ,
  output Imm,
  output MemToReg,
  output RegWrite,
  output jal,
  output jump_jal,
  output jr,
  output bne,
  output beq,
  output MemWrite,
  output lui,
  output Display
);

  Multiplexer #(.select(4), .width(16), .enable("false")) multiplexer_1 (
    .in0(16'h81), .in1(16'h82), .in2(16'h84), .in3(16'h88), .in4(16'hb0), .in5(16'ha0), .in6(16'ha0),
    .in7(16'h380), .in8(16'h200), .in9(16'h400), .in10(16'h1000), .in11(16'h800), .in12(16'h2030),
    .in13(16'h40a0), .in14(16'hf0), .in15(16'h8020),
    .out({Display, lui, MemWrite, beq, bne, jr, jump_jal, jal, RegWrite, MemToReg, Imm, \signed , bc, zb, ffo, RegDst}),
    .sel(opcode));
endmodule

module Exec_Instruction (
  input  [15:0] X,
  input  [15:0] Y,
  input  [3:0] funct,
  input  [3:0] opcode,
  output Signed_Overflow,
  output [15:0] Result,
  output Equal
);

  wire [3:0] multiplexer_1_out, multiplexer_2_out;

  Multiplexer #(.select(4), .width(4)) multiplexer_1 (
    .in0(4'b0000), .in1(4'b0001), .in2(4'b0010), .in3(4'b0011), .in4(4'b0100), .in5(4'b0101), .in6(4'b0110),
    .in7(4'b0111), .out(multiplexer_1_out), .sel(funct));  // open: in8, in9, in10, in11, in12, in13, in14, in15, en
  Multiplexer #(.select(4), .width(4)) multiplexer_2 (
    .in0(multiplexer_1_out), .in4(4'b0110), .in5(4'b0000), .in6(4'b0001), .in12(4'b0110), .in14(4'b0110),
    .out(multiplexer_2_out), .sel(opcode));  // open: in1, in2, in3, in7, in8, in9, in10, in11, in13, in15, en
  alu_main main_1 (
    .switch__S(multiplexer_2_out), .X(X), .equal(Equal), .result(Result), .signed_overflow(Signed_Overflow),
    .Y(Y));
endmodule

module ffo (
  input  [15:0] rs,
  output [15:0] rt
);

  wire bitfinder_1_found;
  wire [3:0] bitfinder_1_index;
  wire [15:0] bit_extender_1_out, subtractor_1_out;

  BitFinder #(.width(16), .\type ("high1")) bitfinder_1 (.in(rs), .index(bitfinder_1_index), .found(bitfinder_1_found));
  assign bit_extender_1_out = {{12{1'b0}}, bitfinder_1_index};  // Bit_Extender bit_extender_1
  Subtractor #(.width(16)) subtractor_1 (.a(16'hf), .b(bit_extender_1_out), .out(subtractor_1_out));  // open: bin, bout
  Multiplexer #(.width(16)) multiplexer_1 (
    .in0(16'h10), .in1(subtractor_1_out), .out(rt), .sel(bitfinder_1_found));  // open: en

  // Notes on the sheet:
  //   ffo
endmodule

module zb (
  input  [15:0] rs,
  output [15:0] rt
);

  wire bitfinder_1_found, bitfinder_2_found, not_1_out, not_2_out, or_1_out;

  BitFinder #(.\type ("high1")) bitfinder_1 (.in(rs[7:0]), .found(bitfinder_1_found));  // open: index
  not not_1 (not_1_out, bitfinder_1_found);
  not not_2 (not_2_out, bitfinder_2_found);
  BitFinder #(.\type ("high1")) bitfinder_2 (.in(rs[15:8]), .found(bitfinder_2_found));  // open: index
  or or_1 (or_1_out, not_1_out, not_2_out);
  assign rt = {{15{1'b0}}, or_1_out};  // Bit_Extender bit_extender_1

  // Notes on the sheet:
  //   zb
endmodule

module bc (
  input  [15:0] rs,
  output [15:0] rt
);

  wire [4:0] bitadder_1_out;

  BitAdder #(.width(1)) bitadder_1 (
    .in0(rs[0]), .in1(rs[1]), .in2(rs[2]), .in3(rs[3]), .in4(rs[4]), .in5(rs[5]), .in6(rs[6]), .in7(rs[7]),
    .in8(rs[8]), .in9(rs[9]), .in10(rs[10]), .in11(rs[11]), .in12(rs[12]), .in13(rs[13]), .in14(rs[14]),
    .in15(rs[15]), .out(bitadder_1_out));
  // Probe on rt
  assign rt = {{11{1'b0}}, bitadder_1_out};  // Bit_Extender bit_extender_1

  // Notes on the sheet:
  //   bc
endmodule
